# Fritzing sketch Fritzing Sketch Source File (saved by Fritzing 0.9.3b)

parts:
  Part1 = Arduino Uno (Rev3) - ICSP
  Part2 = FC-28 Soil Hygrometer Module
  Part4 = richardbruneau00000
  U2 = LCD-16X2 [package=lcd-16x2]
  LCM1602_IIC2 = LCM1602 IIC [part_number="LCM1602 IIC" chip_label="LCM1602 IIC" package="DIP (Dual Inline) [THT]"]
  R1 = Resistor [tolerance=±5% resistance=220 package="0805 [SMD]"]
  LED1 = LED - 3mm [color="Red (633nm)" package="3 mm [THT]"]

nets:
  N1: Part1.A0, Part2.AO
  N2: Part1.A4/SDA, LCM1602_IIC2.SCL
  N3: Part1.A5/SCL, LCM1602_IIC2.SDA
  N4: Part1.D11_PWM/MOSI, R1.Pin_0
  GND: Part1.GND, Part2.GND, LCM1602_IIC2.GND, LED1.cathode
  VCC: Part1.5V, Part2.VCC, LCM1602_IIC2.VCC
  N5: Part2.POS, Part4.connector8
  N6: Part2.NEG, Part4.connector9
  N7: U2.VSS, LCM1602_IIC2.K
  N8: U2.VDD, LCM1602_IIC2.A
  N9: U2.VO, LCM1602_IIC2.D7
  N10: U2.RS, LCM1602_IIC2.D6
  N11: U2.R_W, LCM1602_IIC2.D5
  N12: U2.E, LCM1602_IIC2.D4
  N13: U2.DB0, LCM1602_IIC2.D3
  N14: U2.DB1, LCM1602_IIC2.D2
  N15: U2.DB2, LCM1602_IIC2.D1
  N16: U2.DB3, LCM1602_IIC2.D0
  N17: U2.DB4, LCM1602_IIC2.E
  N18: U2.DB5, LCM1602_IIC2.RW
  N19: U2.DB6, LCM1602_IIC2.RS
  N20: U2.DB7, LCM1602_IIC2.V0
  N21: U2.A, LCM1602_IIC2.VDD
  N22: U2.K, LCM1602_IIC2.VSS

notes:
  GND - Green
  5VC - Red
  GPIO - Blue
  Developed By Web Dev Fusion
  www.webdevfusion.com

custom parts:
  FC-28 Soil Hygrometer Module: The FC-28 is a soil hygrometer module that uses the Texas Instruments LM393 comparator chip to provide an analog measurement of soil humidity. The digital output is high when soil moisture is over a certain threshold, as determined by adjusting the potentiometer.
  LCM1602 IIC: I2C-Module to use a 1602 or 2004 LCD on with the wire.h libory Serial LCD Modul
